// Logisim project cpu.circ as structural Verilog: 1 circuit, main circuit cpu
module cpu (
  input  clk,
  input  [31:0] Instruction,
  input  [31:0] MemReadData,
  output [31:0] MemAddress,
  output [31:0] ProgramCounter,
  output [31:0] ra,
  output [31:0] sp,
  output [31:0] t0,
  output [31:0] t1,
  output [31:0] t2,
  output [31:0] s0,
  output [31:0] s1,
  output [31:0] a0,
  output [3:0] MemWriteMask,
  output [31:0] MemWriteData
);

  wire branch_comp_1_breq, branch_comp_1_brlt, control_logic_1_asel, control_logic_1_brun,
       control_logic_1_bsel, control_logic_1_memwen, control_logic_1_pcsel, control_logic_1_regwen,
       regfile_1_p7, regfile_1_p8, regfile_1_p10, regfile_1_p22, regfile_1_p24;
  wire [1:0] control_logic_1_wbsel;
  wire [2:0] control_logic_1_immsel;
  wire [3:0] control_logic_1_alusel;
  wire [31:0] adder_1_out, DataToReg, imm_gen_1_immediate, multiplexer_1_out, multiplexer_2_out,
       multiplexer_3_out, regfile_1_p4, regfile_1_p19, regfile_1_p20;

  Adder #(.width(32)) adder_1 (.a(ProgramCounter), .b(32'h4), .out(adder_1_out));  // open: cin, cout
  Register #(.width(32)) PC (.D(multiplexer_1_out), .clk(clk), .Q(ProgramCounter));  // open: en, clr
  Multiplexer #(.enable("false"), .width(32)) multiplexer_1 (
    .in0(adder_1_out), .in1(MemAddress), .out(multiplexer_1_out), .sel(control_logic_1_pcsel));
  control_logic control_logic_1 (
    .PCSel(control_logic_1_pcsel), .RegWEn(control_logic_1_regwen), .ImmSel(control_logic_1_immsel),
    .BrUn(control_logic_1_brun), .ASel(control_logic_1_asel), .BSel(control_logic_1_bsel),
    .ALUSel(control_logic_1_alusel), .MemWEn(control_logic_1_memwen), .WBSel(control_logic_1_wbsel),
    .Instruction(Instruction), .BrEq(branch_comp_1_breq), .BrLt(branch_comp_1_brlt));
  // regfile regfile_1: pin names not known; wires that end beside it: Instruction[19:15], Instruction[24:20], Instruction[11:7], regfile_1_p4, control_logic_1_regwen, clk, regfile_1_p7, regfile_1_p8, regfile_1_p8, regfile_1_p10, ra, sp, t0, t1, t2, s0, s1, a0, regfile_1_p19, regfile_1_p20, regfile_1_p10, regfile_1_p22, regfile_1_p22, regfile_1_p24, regfile_1_p24
  imm_gen imm_gen_1 (.Instruction(Instruction), .ImmSel(control_logic_1_immsel), .Immediate(imm_gen_1_immediate));
  branch_comp branch_comp_1 (
    .BrData1(regfile_1_p19), .BrData2(regfile_1_p20), .BrUn(control_logic_1_brun), .BrEq(branch_comp_1_breq),
    .BrLt(branch_comp_1_brlt));
  Multiplexer #(.enable("false"), .width(32)) multiplexer_2 (
    .in0(regfile_1_p20), .in1(imm_gen_1_immediate), .out(multiplexer_2_out), .sel(control_logic_1_bsel));
  Multiplexer #(.enable("false"), .width(32)) multiplexer_3 (
    .in0(regfile_1_p19), .in1(ProgramCounter), .out(multiplexer_3_out), .sel(control_logic_1_asel));
  alu alu_1 (.ALUResult(MemAddress), .A(multiplexer_3_out), .B(multiplexer_2_out), .ALUSel(control_logic_1_alusel));
  partial_store partial_store_1 (
    .Instruction(Instruction), .MemAddress(MemAddress), .DataFromReg(regfile_1_p20),
    .MemWEn(control_logic_1_memwen), .MemWriteMask(MemWriteMask), .DataToMem(MemWriteData));
  Multiplexer #(.enable("false"), .select(2), .width(32)) multiplexer_4 (
    .in0(DataToReg), .in1(MemAddress), .out(regfile_1_p4), .sel(control_logic_1_wbsel));  // open: in2, in3
  partial_load partial_load_1 (
    .Instruction(Instruction), .MemAddress(MemAddress), .DataFromMem(MemReadData), .DataToReg(DataToReg));

  // Notes on the sheet:
  //   To IMEM
  //   IMEM (do **NOT** move this)
  //   From IMEM
  //   Inputs/Outputs for testing. Do **NOT** move these.
  //   To DMEM
  //   DMEM (do **NOT** move this)
  //   From DMEM
endmodule
